// Logisim project ULA32bits.circ as structural Verilog: 16 circuits, main circuit CelulaULA
module COMPUTADOR (
  input  RESET,
  input  [31:0] VISUALIZADOR_S,
  output OVERFLOW,
  output ZERO
);

  wire clock_1_out, not_1_out;
  wire [7:0] microprocessador_1_addrs;
  wire [31:0] ram_1_data;

  Clock clock_1 (.out(clock_1_out));
  not not_1 (not_1_out, clock_1_out);
  RAM #(.dataWidth(32)) ram_1 (.addr(microprocessador_1_addrs), .data(ram_1_data));  // open: sel, clk, ld, clr
  MICROPROCESSADOR microprocessador_1 (
    .CLOCK(clock_1_out), .ENTRADA(ram_1_data), .Addrs(microprocessador_1_addrs), .WR(not_1_out),
    .RESET(RESET), .VISUALIZADOR(VISUALIZADOR_S), .OVERFLOW(OVERFLOW), .ZERO(ZERO));
endmodule

module MICROPROCESSADOR (
  input  CLOCK,
  input  [31:0] ENTRADA,
  input  WR,
  input  RESET,
  output [7:0] Addrs,
  output [31:0] VISUALIZADOR,
  output OVERFLOW,
  output ZERO
);

  wire and_1_out, circuito_jump_1_jump_program_counter;
  wire [31:0] multiplexer_1_out, undriven, undriven_2, undriven_3;

  CirCuito_JUMP circuito_jump_1 (
    .JUMP_Program_Counter(circuito_jump_1_jump_program_counter), .OPcode_ULA(ENTRADA[31:27]), .ZERO(OVERFLOW));
  PROGRAM_COUNTER program_counter_1 (
    .RESET(RESET), .CLK(CLOCK), .Deslocamento_PC(ENTRADA[7:0]), .JUMP(circuito_jump_1_jump_program_counter),
    .out_5(Addrs));
  Gambiarra_12___32 gambiarra_12_32_1 (.out_2(ENTRADA[11:0]), .in_1(undriven_2));
  BANCOREG bancoreg_1 (
    .WR(WR), .DATA(VISUALIZADOR), .OP___RS(ENTRADA[21:17]), .OP___RT(ENTRADA[16:12]), .RSOut(undriven_3),
    .RTOut(undriven), .REGDESTINO(ENTRADA[26:22]));
  Multiplexer #(.width(32), .enable("false")) multiplexer_1 (
    .in0(undriven), .in1(undriven_2), .out(multiplexer_1_out), .sel(and_1_out));
  and and_1 (and_1_out, ~ENTRADA[31], ENTRADA[30], ENTRADA[29], ~ENTRADA[28], ~ENTRADA[27]);  // AND_Gate
  ULA ula_1 (
    .OPCode(ENTRADA[31:27]), .A(undriven_3), .B(multiplexer_1_out), .out_6(ZERO), .S(VISUALIZADOR),
    .OVERFLOW(OVERFLOW));

  // Notes on the sheet:
  //   ULA
  //   1
  //   Destin
  //   Reg. S
  //   2
  //   3
  //   Reg. T
  //   4
  //   Constante
endmodule

module CASAMENTO (
  input  [4:0] RSOUT,
  input  [4:0] opcode,
  input  [4:0] RTOUT,
  input  [11:0] DataIN,
  input  [4:0] REGDEST,
  input  WR,
  output [31:0] out_7,
  output OVERFLOW,
  output S0,
  output out_10
);

  wire [31:0] multiplexer_1_out, undriven, undriven_2, undriven_3;

  Gambiarra_12___32 gambiarra_12_32_1 (.out_2(DataIN), .in_1(undriven));
  BANCOREG bancoreg_1 (
    .WR(WR), .DATA(out_7), .OP___RS(RSOUT), .OP___RT(RTOUT), .RSOut(undriven_2), .RTOut(undriven_3),
    .REGDESTINO(REGDEST));
  Multiplexer #(.width(32), .enable("false")) multiplexer_1 (
    .in0(undriven_3), .in1(undriven), .out(multiplexer_1_out), .sel(out_10));
  ULA ula_1 (.OPCode(opcode), .A(undriven_2), .B(multiplexer_1_out), .out_6(S0), .S(out_7), .OVERFLOW(OVERFLOW));
endmodule

module ULA (
  input  [31:0] A,
  input  [31:0] B,
  input  [4:0] OPCode,
  output [31:0] S,
  output OVERFLOW,
  output out_6
);

  wire _0_cout, _1_cout, _2_cout, _3_cout, _4_cout, _5_cout, _6_cout, _7_cout, _8_cout, _9_cout, _10_cout,
       _11_cout, _12_cout, _13_cout, _14_cout, _15_cout, _16_cout, _17_cout, _18_cout, _19_cout, _20_cout,
       _21_cout, _22_cout, _23_cout, _24_cout, _25_cout, _26_cout, _27_cout, _28_cout, _29_cout, _30_cout,
       _31_cout, and_1_out, and_2_out, LEFT_out, RIGTH_out, rol_1_s0, rol_1_s1, rol_1_s2, rol_1_s3, rol_1_s4,
       rol_1_s5, rol_1_s6, rol_1_s7, rol_1_s8, rol_1_s9, rol_1_s10, rol_1_s11, rol_1_s12, rol_1_s13,
       rol_1_s14, rol_1_s15, rol_1_s16, rol_1_s17, rol_1_s18, rol_1_s19, rol_1_s20, rol_1_s21, rol_1_s22,
       rol_1_s23, rol_1_s24, rol_1_s25, rol_1_s26, rol_1_s27, rol_1_s28, rol_1_s29, rol_1_s30, rol_1_s31,
       shifter_aritimetico_1_s0, shifter_aritimetico_1_s1, shifter_aritimetico_1_s2,
       shifter_aritimetico_1_s3, shifter_aritimetico_1_s4, shifter_aritimetico_1_s5,
       shifter_aritimetico_1_s6, shifter_aritimetico_1_s7, shifter_aritimetico_1_s8,
       shifter_aritimetico_1_s9, shifter_aritimetico_1_s10, shifter_aritimetico_1_s11,
       shifter_aritimetico_1_s12, shifter_aritimetico_1_s13, shifter_aritimetico_1_s14,
       shifter_aritimetico_1_s15, shifter_aritimetico_1_s16, shifter_aritimetico_1_s17,
       shifter_aritimetico_1_s18, shifter_aritimetico_1_s19, shifter_aritimetico_1_s20,
       shifter_aritimetico_1_s21, shifter_aritimetico_1_s22, shifter_aritimetico_1_s23,
       shifter_aritimetico_1_s24, shifter_aritimetico_1_s25, shifter_aritimetico_1_s26,
       shifter_aritimetico_1_s27, shifter_aritimetico_1_s28, shifter_aritimetico_1_s29,
       shifter_aritimetico_1_s30, shifter_aritimetico_1_s31, SHIFTER_s0, SHIFTER_s1, SHIFTER_s2, SHIFTER_s3,
       SHIFTER_s4, SHIFTER_s5, SHIFTER_s6, SHIFTER_s7, SHIFTER_s8, SHIFTER_s9, SHIFTER_s10, SHIFTER_s11,
       SHIFTER_s12, SHIFTER_s13, SHIFTER_s14, SHIFTER_s15, SHIFTER_s16, SHIFTER_s17, SHIFTER_s18,
       SHIFTER_s19, SHIFTER_s20, SHIFTER_s21, SHIFTER_s22, SHIFTER_s23, SHIFTER_s24, SHIFTER_s25,
       SHIFTER_s26, SHIFTER_s27, SHIFTER_s28, SHIFTER_s29, SHIFTER_s30, SHIFTER_s31;
  wire [31:0] not_1_out;

  and LEFT (LEFT_out, ~OPCode[4], ~OPCode[3], OPCode[2], OPCode[1], ~OPCode[0]);  // AND_Gate
  CelulaULA _28 (.S(S[28]), .A(rol_1_s28), .B(B[28]), .Seletor(OPCode), .Cin(_27_cout), .Cout(_28_cout));
  and RIGTH (RIGTH_out, ~OPCode[4], ~OPCode[3], OPCode[2], OPCode[1], OPCode[0]);  // AND_Gate
  and and_1 (and_1_out, ~OPCode[4], OPCode[3], ~OPCode[2], ~OPCode[1], OPCode[0]);  // AND_Gate
  and and_2 (and_2_out, ~OPCode[4], OPCode[3], ~OPCode[2], OPCode[1], ~OPCode[0]);  // AND_Gate
  SHIFTER SHIFTER (
    .SHFLEFT(LEFT_out), .SHFRIGTH(RIGTH_out), .A31(A[31]), .A30(A[30]), .A29(A[29]), .A28(A[28]),
    .A27(A[27]), .A26(A[26]), .A25(A[25]), .A24(A[24]), .A23(A[23]), .A22(A[22]), .A21(A[21]), .A20(A[20]),
    .A19(A[19]), .A18(A[18]), .A17(A[17]), .A16(A[16]), .A15(A[15]), .A14(A[14]), .A13(A[13]), .A12(A[12]),
    .A11(A[11]), .A10(A[10]), .A9(A[9]), .A8(A[8]), .A7(A[7]), .A6(A[6]), .A5(A[5]), .A4(A[4]), .A3(A[3]),
    .A2(A[2]), .A1(A[1]), .A0(A[0]), .S31(SHIFTER_s31), .S30(SHIFTER_s30), .S29(SHIFTER_s29),
    .S28(SHIFTER_s28), .S27(SHIFTER_s27), .S26(SHIFTER_s26), .S25(SHIFTER_s25), .S24(SHIFTER_s24),
    .S23(SHIFTER_s23), .S22(SHIFTER_s22), .S21(SHIFTER_s21), .S20(SHIFTER_s20), .S19(SHIFTER_s19),
    .S18(SHIFTER_s18), .S17(SHIFTER_s17), .S16(SHIFTER_s16), .S15(SHIFTER_s15), .S14(SHIFTER_s14),
    .S13(SHIFTER_s13), .S12(SHIFTER_s12), .S11(SHIFTER_s11), .S10(SHIFTER_s10), .S9(SHIFTER_s9),
    .S8(SHIFTER_s8), .S7(SHIFTER_s7), .S6(SHIFTER_s6), .S5(SHIFTER_s5), .S4(SHIFTER_s4), .S3(SHIFTER_s3),
    .S2(SHIFTER_s2), .S1(SHIFTER_s1), .S0(SHIFTER_s0));
  SHIFTER_ARITIMETICO shifter_aritimetico_1 (
    .in_33(and_1_out), .A31(SHIFTER_s31), .A30(SHIFTER_s30), .A29(SHIFTER_s29), .A28(SHIFTER_s28),
    .A27(SHIFTER_s27), .A26(SHIFTER_s26), .A25(SHIFTER_s25), .A24(SHIFTER_s24), .A23(SHIFTER_s23),
    .A22(SHIFTER_s22), .A21(SHIFTER_s21), .A20(SHIFTER_s20), .A19(SHIFTER_s19), .A18(SHIFTER_s18),
    .A17(SHIFTER_s17), .A16(SHIFTER_s16), .A15(SHIFTER_s15), .A14(SHIFTER_s14), .A13(SHIFTER_s13),
    .A12(SHIFTER_s12), .A11(SHIFTER_s11), .A10(SHIFTER_s10), .A9(SHIFTER_s9), .A8(SHIFTER_s8),
    .A7(SHIFTER_s7), .A6(SHIFTER_s6), .A5(SHIFTER_s5), .A4(SHIFTER_s4), .A3(SHIFTER_s3), .A2(SHIFTER_s2),
    .A1(SHIFTER_s1), .A0(SHIFTER_s0), .S31(shifter_aritimetico_1_s31), .S30(shifter_aritimetico_1_s30),
    .S29(shifter_aritimetico_1_s29), .S28(shifter_aritimetico_1_s28), .S27(shifter_aritimetico_1_s27),
    .S26(shifter_aritimetico_1_s26), .S25(shifter_aritimetico_1_s25), .S24(shifter_aritimetico_1_s24),
    .S23(shifter_aritimetico_1_s23), .S22(shifter_aritimetico_1_s22), .S21(shifter_aritimetico_1_s21),
    .S20(shifter_aritimetico_1_s20), .S19(shifter_aritimetico_1_s19), .S18(shifter_aritimetico_1_s18),
    .S17(shifter_aritimetico_1_s17), .S16(shifter_aritimetico_1_s16), .S15(shifter_aritimetico_1_s15),
    .S14(shifter_aritimetico_1_s14), .S13(shifter_aritimetico_1_s13), .S12(shifter_aritimetico_1_s12),
    .S11(shifter_aritimetico_1_s11), .S10(shifter_aritimetico_1_s10), .S9(shifter_aritimetico_1_s9),
    .S8(shifter_aritimetico_1_s8), .S7(shifter_aritimetico_1_s7), .S6(shifter_aritimetico_1_s6),
    .S5(shifter_aritimetico_1_s5), .S4(shifter_aritimetico_1_s4), .S3(shifter_aritimetico_1_s3),
    .S2(shifter_aritimetico_1_s2), .S1(shifter_aritimetico_1_s1), .S0(shifter_aritimetico_1_s0));
  ROL rol_1 (
    .in_33(and_2_out), .A31(shifter_aritimetico_1_s31), .A30(shifter_aritimetico_1_s30),
    .A29(shifter_aritimetico_1_s29), .A28(shifter_aritimetico_1_s28), .A27(shifter_aritimetico_1_s27),
    .A26(shifter_aritimetico_1_s26), .A25(shifter_aritimetico_1_s25), .A24(shifter_aritimetico_1_s24),
    .A23(shifter_aritimetico_1_s23), .A22(shifter_aritimetico_1_s22), .A21(shifter_aritimetico_1_s21),
    .A20(shifter_aritimetico_1_s20), .A19(shifter_aritimetico_1_s19), .A18(shifter_aritimetico_1_s18),
    .A17(shifter_aritimetico_1_s17), .A16(shifter_aritimetico_1_s16), .A15(shifter_aritimetico_1_s15),
    .A14(shifter_aritimetico_1_s14), .A13(shifter_aritimetico_1_s13), .A12(shifter_aritimetico_1_s12),
    .A11(shifter_aritimetico_1_s11), .A10(shifter_aritimetico_1_s10), .A9(shifter_aritimetico_1_s9),
    .A8(shifter_aritimetico_1_s8), .A7(shifter_aritimetico_1_s7), .A6(shifter_aritimetico_1_s6),
    .A5(shifter_aritimetico_1_s5), .A4(shifter_aritimetico_1_s4), .A3(shifter_aritimetico_1_s3),
    .A2(shifter_aritimetico_1_s2), .A1(shifter_aritimetico_1_s1), .A0(shifter_aritimetico_1_s0),
    .S31(rol_1_s31), .S30(rol_1_s30), .S29(rol_1_s29), .S28(rol_1_s28), .S27(rol_1_s27), .S26(rol_1_s26),
    .S25(rol_1_s25), .S24(rol_1_s24), .S23(rol_1_s23), .S22(rol_1_s22), .S21(rol_1_s21), .S20(rol_1_s20),
    .S19(rol_1_s19), .S18(rol_1_s18), .S17(rol_1_s17), .S16(rol_1_s16), .S15(rol_1_s15), .S14(rol_1_s14),
    .S13(rol_1_s13), .S12(rol_1_s12), .S11(rol_1_s11), .S10(rol_1_s10), .S9(rol_1_s9), .S8(rol_1_s8),
    .S7(rol_1_s7), .S6(rol_1_s6), .S5(rol_1_s5), .S4(rol_1_s4), .S3(rol_1_s3), .S2(rol_1_s2), .S1(rol_1_s1),
    .S0(rol_1_s0));
  CelulaULA _29 (.S(S[29]), .A(rol_1_s29), .B(B[29]), .Seletor(OPCode), .Cin(_28_cout), .Cout(_29_cout));
  CelulaULA _24 (.S(S[24]), .A(rol_1_s24), .B(B[24]), .Seletor(OPCode), .Cin(_23_cout), .Cout(_24_cout));
  CelulaULA _25 (.S(S[25]), .A(rol_1_s25), .B(B[25]), .Seletor(OPCode), .Cin(_24_cout), .Cout(_25_cout));
  CelulaULA _26 (.S(S[26]), .A(rol_1_s26), .B(B[26]), .Seletor(OPCode), .Cin(_25_cout), .Cout(_26_cout));
  CelulaULA _27 (.S(S[27]), .A(rol_1_s27), .B(B[27]), .Seletor(OPCode), .Cin(_26_cout), .Cout(_27_cout));
  CelulaULA _30 (.S(S[30]), .A(rol_1_s30), .B(B[30]), .Seletor(OPCode), .Cin(_29_cout), .Cout(_30_cout));
  CelulaULA _31 (.S(S[31]), .A(rol_1_s31), .B(B[31]), .Seletor(OPCode), .Cin(_30_cout), .Cout(_31_cout));
  CelulaULA _23 (.S(S[23]), .A(rol_1_s23), .B(B[23]), .Seletor(OPCode), .Cin(_22_cout), .Cout(_23_cout));
  CelulaULA _22 (.S(S[22]), .A(rol_1_s22), .B(B[22]), .Seletor(OPCode), .Cin(_21_cout), .Cout(_22_cout));
  CelulaULA _21 (.S(S[21]), .A(rol_1_s21), .B(B[21]), .Seletor(OPCode), .Cin(_20_cout), .Cout(_21_cout));
  CelulaULA _20 (.S(S[20]), .A(rol_1_s20), .B(B[20]), .Seletor(OPCode), .Cin(_19_cout), .Cout(_20_cout));
  CelulaULA _16 (.S(S[16]), .A(rol_1_s16), .B(B[16]), .Seletor(OPCode), .Cin(_15_cout), .Cout(_16_cout));
  CelulaULA _17 (.S(S[17]), .A(rol_1_s17), .B(B[17]), .Seletor(OPCode), .Cin(_16_cout), .Cout(_17_cout));
  CelulaULA _18 (.S(S[18]), .A(rol_1_s18), .B(B[18]), .Seletor(OPCode), .Cin(_17_cout), .Cout(_18_cout));
  CelulaULA _19 (.S(S[19]), .A(rol_1_s19), .B(B[19]), .Seletor(OPCode), .Cin(_18_cout), .Cout(_19_cout));
  OverFlowCONTROLER overflowcontroler_1 (
    .OverFlow(OVERFLOW), .CoutMSB(_31_cout), .a(rol_1_s31), .b(B[31]), .s(S[31]), .OPcode(OPCode));
  assign not_1_out = ~S;  // NOT_Gate not_1, 32 bits wide
  and and_3 (out_6, not_1_out[16], not_1_out[31], not_1_out[30], not_1_out[29], not_1_out[28], not_1_out[27], not_1_out[26], not_1_out[25], not_1_out[24], not_1_out[23], not_1_out[22], not_1_out[21], not_1_out[20], not_1_out[19], not_1_out[18], not_1_out[17], not_1_out[15], not_1_out[14], not_1_out[13], not_1_out[12], not_1_out[11], not_1_out[10], not_1_out[9], not_1_out[8], not_1_out[7], not_1_out[6], not_1_out[5], not_1_out[4], not_1_out[3], not_1_out[2], not_1_out[1], not_1_out[0]);
  CelulaULA _15 (.S(S[15]), .A(rol_1_s15), .B(B[15]), .Seletor(OPCode), .Cin(_14_cout), .Cout(_15_cout));
  CelulaULA _14 (.S(S[14]), .A(rol_1_s14), .B(B[14]), .Seletor(OPCode), .Cin(_13_cout), .Cout(_14_cout));
  CelulaULA _13 (.S(S[13]), .A(rol_1_s13), .B(B[13]), .Seletor(OPCode), .Cin(_12_cout), .Cout(_13_cout));
  CelulaULA _12 (.S(S[12]), .A(rol_1_s12), .B(B[12]), .Seletor(OPCode), .Cin(_11_cout), .Cout(_12_cout));
  CelulaULA _8 (.S(S[8]), .A(rol_1_s8), .B(B[8]), .Seletor(OPCode), .Cin(_7_cout), .Cout(_8_cout));
  CelulaULA _9 (.S(S[9]), .A(rol_1_s9), .B(B[9]), .Seletor(OPCode), .Cin(_8_cout), .Cout(_9_cout));
  CelulaULA _10 (.S(S[10]), .A(rol_1_s10), .B(B[10]), .Seletor(OPCode), .Cin(_9_cout), .Cout(_10_cout));
  CelulaULA _11 (.S(S[11]), .A(rol_1_s11), .B(B[11]), .Seletor(OPCode), .Cin(_10_cout), .Cout(_11_cout));
  CelulaULA _7 (.S(S[7]), .A(rol_1_s7), .B(B[7]), .Seletor(OPCode), .Cin(_6_cout), .Cout(_7_cout));
  CelulaULA _6 (.S(S[6]), .A(rol_1_s6), .B(B[6]), .Seletor(OPCode), .Cin(_5_cout), .Cout(_6_cout));
  CelulaULA _5 (.S(S[5]), .A(rol_1_s5), .B(B[5]), .Seletor(OPCode), .Cin(_4_cout), .Cout(_5_cout));
  CelulaULA _4 (.S(S[4]), .A(rol_1_s4), .B(B[4]), .Seletor(OPCode), .Cin(_3_cout), .Cout(_4_cout));
  CelulaULA _0 (.S(S[0]), .A(rol_1_s0), .B(B[0]), .Seletor(OPCode), .Cin(1'b0), .Cout(_0_cout));
  CelulaULA _1 (.S(S[1]), .A(rol_1_s1), .B(B[1]), .Seletor(OPCode), .Cin(_0_cout), .Cout(_1_cout));
  CelulaULA _2 (.S(S[2]), .A(rol_1_s2), .B(B[2]), .Seletor(OPCode), .Cin(_1_cout), .Cout(_2_cout));
  CelulaULA _3 (.S(S[3]), .A(rol_1_s3), .B(B[3]), .Seletor(OPCode), .Cin(_2_cout), .Cout(_3_cout));
endmodule

// 00 - AND
module CelulaULA (
  input  A,
  input  B,
  input  Cin,
  input  [4:0] Seletor,
  output S,
  output Cout
);

  wire adder_1_cout, adder_1_out, and_1_out, and_2_out, nand_1_out, or_1_out, subtractor_1_bout,
       subtractor_1_out, xor_1_out;

  and and_1 (and_1_out, A, B);
  or or_1 (or_1_out, A, B);
  xor xor_1 (xor_1_out, A, B);
  nand nand_1 (nand_1_out, A, B);
  Adder #(.width(1)) adder_1 (.a(A), .b(B), .out(adder_1_out), .cin(Cin), .cout(adder_1_cout));
  Subtractor #(.width(1)) subtractor_1 (.a(A), .b(B), .out(subtractor_1_out), .bin(Cin), .bout(subtractor_1_bout));
  and and_2 (and_2_out, ~Seletor[4], ~Seletor[3], Seletor[2], Seletor[1], ~Seletor[0]);  // AND_Gate
  Multiplexer #(.enable("false")) multiplexer_1 (
    .in0(adder_1_cout), .in1(subtractor_1_bout), .out(Cout), .sel(and_2_out));
  Multiplexer #(.select(5), .enable("false")) multiplexer_2 (
    .in0(and_1_out), .in1(or_1_out), .in2(xor_1_out), .in3(nand_1_out), .in4(adder_1_out), .in5(adder_1_out),
    .in6(subtractor_1_out), .in7(A), .in8(A), .in9(A), .in10(A), .out(S), .sel(Seletor));  // open: in11, in12, in13, in14, in15, in16, in17, in18, in19, in20, in21, in22, in23, in24, in25, in26, in27, in28, in29, in30, in31

  // Notes on the sheet:
  //   01 - OR
  //   1010 - ROL
  //   00 - AND
  //   10 - XOR
  //   11 - NAND
  //   100 - SOMA NAT
  //   101 - SOMA INT
  //   110 - SUBTRAÇÃO
  //   1001 - DIREITA ARITIMETICO
  //   111 - DESLOCAMENTO DIR(SRL)
  //   1000 - DESLOCAMENTO ESQ(SLL)
endmodule

module PROGRAM_COUNTER (
  input  RESET,
  input  CLK,
  input  [7:0] Deslocamento_PC,
  input  JUMP,
  output [7:0] out_5
);

  wire [7:0] adder_1_out, multiplexer_1_out;

  Multiplexer #(.width(8), .enable("false")) multiplexer_1 (
    .in0(8'h1), .in1(Deslocamento_PC), .out(multiplexer_1_out), .sel(JUMP));
  Register register_1 (.D(adder_1_out), .Q(out_5), .clk(CLK), .clr(RESET));  // open: en
  Adder adder_1 (.a(out_5), .b(multiplexer_1_out), .out(adder_1_out), .cin(1'b0));  // open: cout
endmodule

// BREG
module BANCOREG (
  input  [4:0] REGDESTINO,
  input  WR,
  input  [31:0] RSOut,
  input  [31:0] RTOut,
  input  [31:0] DATA,
  output [4:0] OP___RS,
  output [4:0] OP___RT
);

  wire demultiplexer_1_out1, demultiplexer_1_out2, demultiplexer_1_out3, demultiplexer_1_out4,
       demultiplexer_1_out5, demultiplexer_1_out6, demultiplexer_1_out7, demultiplexer_1_out8,
       demultiplexer_1_out9, demultiplexer_1_out10, demultiplexer_1_out11, demultiplexer_1_out12,
       demultiplexer_1_out13, demultiplexer_1_out14, demultiplexer_1_out15, demultiplexer_1_out16,
       demultiplexer_1_out17, demultiplexer_1_out18, demultiplexer_1_out19, demultiplexer_1_out20,
       demultiplexer_1_out21, demultiplexer_1_out22, demultiplexer_1_out23, demultiplexer_1_out24,
       demultiplexer_1_out25, demultiplexer_1_out26, demultiplexer_1_out27, demultiplexer_1_out28,
       demultiplexer_1_out29, demultiplexer_1_out30, demultiplexer_1_out31;
  wire [31:0] reg_1_dataout, reg_1_resultdatain, reg_2_dataout, reg_2_resultdatain, reg_3_dataout,
       reg_3_resultdatain, reg_4_dataout, reg_4_resultdatain, reg_5_dataout, reg_5_resultdatain,
       reg_6_dataout, reg_6_resultdatain, reg_7_dataout, reg_7_resultdatain, reg_8_dataout,
       reg_8_resultdatain, reg_9_dataout, reg_9_resultdatain, reg_10_dataout, reg_10_resultdatain,
       reg_11_dataout, reg_11_resultdatain, reg_12_dataout, reg_12_resultdatain, reg_13_dataout,
       reg_13_resultdatain, reg_14_dataout, reg_14_resultdatain, reg_15_dataout, reg_15_resultdatain,
       reg_16_dataout, reg_16_resultdatain, reg_17_dataout, reg_17_resultdatain, reg_18_dataout,
       reg_18_resultdatain, reg_19_dataout, reg_19_resultdatain, reg_20_dataout, reg_20_resultdatain,
       reg_21_dataout, reg_21_resultdatain, reg_22_dataout, reg_22_resultdatain, reg_23_dataout,
       reg_23_resultdatain, reg_24_dataout, reg_24_resultdatain, reg_25_dataout, reg_25_resultdatain,
       reg_26_dataout, reg_26_resultdatain, reg_27_dataout, reg_27_resultdatain, reg_28_dataout,
       reg_28_resultdatain, reg_29_dataout, reg_29_resultdatain, reg_30_dataout, reg_30_resultdatain,
       reg_31_resultdatain, undriven, undriven_2;

  REG reg_1 (
    .DATAIN(undriven_2), .DATAOUT(reg_1_dataout), .WR(demultiplexer_1_out1), .resultDATAIN(reg_1_resultdatain));
  REG reg_2 (
    .DATAIN(reg_1_dataout), .DATAOUT(reg_2_dataout), .WR(demultiplexer_1_out2),
    .resultDATAIN(reg_2_resultdatain));
  REG reg_3 (
    .DATAIN(reg_2_dataout), .DATAOUT(reg_3_dataout), .WR(demultiplexer_1_out3),
    .resultDATAIN(reg_3_resultdatain));
  REG reg_4 (
    .DATAIN(reg_3_dataout), .DATAOUT(reg_4_dataout), .WR(demultiplexer_1_out4),
    .resultDATAIN(reg_4_resultdatain));
  Demultiplexer #(.select(5), .enable("false")) demultiplexer_1 (
    .out1(demultiplexer_1_out1), .out2(demultiplexer_1_out2), .out3(demultiplexer_1_out3),
    .out4(demultiplexer_1_out4), .out5(demultiplexer_1_out5), .out6(demultiplexer_1_out6),
    .out7(demultiplexer_1_out7), .out8(demultiplexer_1_out8), .out9(demultiplexer_1_out9),
    .out10(demultiplexer_1_out10), .out11(demultiplexer_1_out11), .out12(demultiplexer_1_out12),
    .out13(demultiplexer_1_out13), .out14(demultiplexer_1_out14), .out15(demultiplexer_1_out15),
    .out16(demultiplexer_1_out16), .out17(demultiplexer_1_out17), .out18(demultiplexer_1_out18),
    .out19(demultiplexer_1_out19), .out20(demultiplexer_1_out20), .out21(demultiplexer_1_out21),
    .out22(demultiplexer_1_out22), .out23(demultiplexer_1_out23), .out24(demultiplexer_1_out24),
    .out25(demultiplexer_1_out25), .out26(demultiplexer_1_out26), .out27(demultiplexer_1_out27),
    .out28(demultiplexer_1_out28), .out29(demultiplexer_1_out29), .out30(demultiplexer_1_out30),
    .out31(demultiplexer_1_out31), .in(WR), .sel(REGDESTINO));  // open: out0
  REG reg_5 (
    .DATAIN(reg_4_dataout), .DATAOUT(reg_5_dataout), .WR(demultiplexer_1_out5),
    .resultDATAIN(reg_5_resultdatain));
  REG reg_6 (
    .DATAIN(reg_5_dataout), .DATAOUT(reg_6_dataout), .WR(demultiplexer_1_out6),
    .resultDATAIN(reg_6_resultdatain));
  REG reg_7 (
    .DATAIN(reg_6_dataout), .DATAOUT(reg_7_dataout), .WR(demultiplexer_1_out7),
    .resultDATAIN(reg_7_resultdatain));
  REG reg_8 (
    .DATAIN(reg_7_dataout), .DATAOUT(reg_8_dataout), .WR(demultiplexer_1_out8),
    .resultDATAIN(reg_8_resultdatain));
  Multiplexer #(.select(5), .width(32), .enable("false")) multiplexer_1 (
    .in0(undriven), .in1(reg_1_resultdatain), .in2(reg_2_resultdatain), .in3(reg_3_resultdatain),
    .in4(reg_4_resultdatain), .in5(reg_5_resultdatain), .in6(reg_6_resultdatain), .in7(reg_7_resultdatain),
    .in8(reg_8_resultdatain), .in9(reg_9_resultdatain), .in10(reg_10_resultdatain),
    .in11(reg_11_resultdatain), .in12(reg_12_resultdatain), .in13(reg_13_resultdatain),
    .in14(reg_14_resultdatain), .in15(reg_15_resultdatain), .in16(reg_16_resultdatain),
    .in17(reg_17_resultdatain), .in18(reg_18_resultdatain), .in19(reg_19_resultdatain),
    .in20(reg_20_resultdatain), .in21(reg_21_resultdatain), .in22(reg_22_resultdatain),
    .in23(reg_23_resultdatain), .in24(reg_24_resultdatain), .in25(reg_25_resultdatain),
    .in26(reg_26_resultdatain), .in27(reg_27_resultdatain), .in28(reg_28_resultdatain),
    .in29(reg_29_resultdatain), .in30(reg_30_resultdatain), .in31(reg_31_resultdatain), .out(RSOut),
    .sel(OP___RS));
  REG reg_9 (
    .DATAIN(reg_8_dataout), .DATAOUT(reg_9_dataout), .WR(demultiplexer_1_out9),
    .resultDATAIN(reg_9_resultdatain));
  REG reg_10 (
    .DATAIN(reg_9_dataout), .DATAOUT(reg_10_dataout), .WR(demultiplexer_1_out10),
    .resultDATAIN(reg_10_resultdatain));
  REG reg_11 (
    .DATAIN(reg_10_dataout), .DATAOUT(reg_11_dataout), .WR(demultiplexer_1_out11),
    .resultDATAIN(reg_11_resultdatain));
  REG reg_12 (
    .DATAIN(reg_11_dataout), .DATAOUT(reg_12_dataout), .WR(demultiplexer_1_out12),
    .resultDATAIN(reg_12_resultdatain));
  REG_0 reg_0_1 (.in_1(DATA), .in_3(undriven_2), .S(undriven));
  REG reg_13 (
    .DATAIN(reg_12_dataout), .DATAOUT(reg_13_dataout), .WR(demultiplexer_1_out13),
    .resultDATAIN(reg_13_resultdatain));
  REG reg_14 (
    .DATAIN(reg_13_dataout), .DATAOUT(reg_14_dataout), .WR(demultiplexer_1_out14),
    .resultDATAIN(reg_14_resultdatain));
  REG reg_15 (
    .DATAIN(reg_14_dataout), .DATAOUT(reg_15_dataout), .WR(demultiplexer_1_out15),
    .resultDATAIN(reg_15_resultdatain));
  REG reg_16 (
    .DATAIN(reg_15_dataout), .DATAOUT(reg_16_dataout), .WR(demultiplexer_1_out16),
    .resultDATAIN(reg_16_resultdatain));
  REG reg_17 (
    .DATAIN(reg_16_dataout), .DATAOUT(reg_17_dataout), .WR(demultiplexer_1_out17),
    .resultDATAIN(reg_17_resultdatain));
  REG reg_18 (
    .DATAIN(reg_17_dataout), .DATAOUT(reg_18_dataout), .WR(demultiplexer_1_out18),
    .resultDATAIN(reg_18_resultdatain));
  REG reg_19 (
    .DATAIN(reg_18_dataout), .DATAOUT(reg_19_dataout), .WR(demultiplexer_1_out19),
    .resultDATAIN(reg_19_resultdatain));
  REG reg_20 (
    .DATAIN(reg_19_dataout), .DATAOUT(reg_20_dataout), .WR(demultiplexer_1_out20),
    .resultDATAIN(reg_20_resultdatain));
  REG reg_21 (
    .DATAIN(reg_20_dataout), .DATAOUT(reg_21_dataout), .WR(demultiplexer_1_out21),
    .resultDATAIN(reg_21_resultdatain));
  REG reg_22 (
    .DATAIN(reg_21_dataout), .DATAOUT(reg_22_dataout), .WR(demultiplexer_1_out22),
    .resultDATAIN(reg_22_resultdatain));
  Multiplexer #(.select(5), .width(32), .enable("false")) multiplexer_2 (
    .in0(undriven), .in1(reg_1_resultdatain), .in2(reg_2_resultdatain), .in3(reg_3_resultdatain),
    .in4(reg_4_resultdatain), .in5(reg_5_resultdatain), .in6(reg_6_resultdatain), .in7(reg_7_resultdatain),
    .in8(reg_8_resultdatain), .in9(reg_9_resultdatain), .in10(reg_10_resultdatain),
    .in11(reg_11_resultdatain), .in12(reg_12_resultdatain), .in13(reg_13_resultdatain),
    .in14(reg_14_resultdatain), .in15(reg_15_resultdatain), .in16(reg_16_resultdatain),
    .in17(reg_17_resultdatain), .in18(reg_18_resultdatain), .in19(reg_19_resultdatain),
    .in20(reg_20_resultdatain), .in21(reg_21_resultdatain), .in22(reg_22_resultdatain),
    .in23(reg_23_resultdatain), .in24(reg_24_resultdatain), .in25(reg_25_resultdatain),
    .in26(reg_26_resultdatain), .in27(reg_27_resultdatain), .in28(reg_28_resultdatain),
    .in29(reg_29_resultdatain), .in30(reg_30_resultdatain), .in31(reg_31_resultdatain), .out(RTOut),
    .sel(OP___RT));
  REG reg_23 (
    .DATAIN(reg_22_dataout), .DATAOUT(reg_23_dataout), .WR(demultiplexer_1_out23),
    .resultDATAIN(reg_23_resultdatain));
  REG reg_24 (
    .DATAIN(reg_23_dataout), .DATAOUT(reg_24_dataout), .WR(demultiplexer_1_out24),
    .resultDATAIN(reg_24_resultdatain));
  REG reg_25 (
    .DATAIN(reg_24_dataout), .DATAOUT(reg_25_dataout), .WR(demultiplexer_1_out25),
    .resultDATAIN(reg_25_resultdatain));
  REG reg_26 (
    .DATAIN(reg_25_dataout), .DATAOUT(reg_26_dataout), .WR(demultiplexer_1_out26),
    .resultDATAIN(reg_26_resultdatain));
  REG reg_27 (
    .DATAIN(reg_26_dataout), .DATAOUT(reg_27_dataout), .WR(demultiplexer_1_out27),
    .resultDATAIN(reg_27_resultdatain));
  REG reg_28 (
    .DATAIN(reg_27_dataout), .DATAOUT(reg_28_dataout), .WR(demultiplexer_1_out28),
    .resultDATAIN(reg_28_resultdatain));
  REG reg_29 (
    .DATAIN(reg_28_dataout), .DATAOUT(reg_29_dataout), .WR(demultiplexer_1_out29),
    .resultDATAIN(reg_29_resultdatain));
  REG reg_30 (
    .DATAIN(reg_29_dataout), .DATAOUT(reg_30_dataout), .WR(demultiplexer_1_out30),
    .resultDATAIN(reg_30_resultdatain));
  REG reg_31 (
    .DATAIN(reg_30_dataout), .WR(demultiplexer_1_out31), .resultDATAIN(reg_31_resultdatain));  // open: DATAOUT
endmodule

module REG (
  input  [31:0] DATAIN,
  input  WR,
  output [31:0] resultDATAIN,
  output [31:0] DATAOUT
);

  D_Flip_Flop d_ff_1 (.clk(WR), .D(DATAIN[0]), .Q(resultDATAIN[0]));  // open: Qn, preset, en, reset
  D_Flip_Flop d_ff_2 (.clk(WR), .D(DATAIN[1]), .Q(resultDATAIN[1]));  // open: Qn, preset, en, reset
  D_Flip_Flop d_ff_3 (.clk(WR), .D(DATAIN[2]), .Q(resultDATAIN[2]));  // open: Qn, preset, en, reset
  D_Flip_Flop d_ff_4 (.clk(WR), .D(DATAIN[3]), .Q(resultDATAIN[3]));  // open: Qn, preset, en, reset
  D_Flip_Flop d_ff_5 (.clk(WR), .D(DATAIN[4]), .Q(resultDATAIN[4]));  // open: Qn, preset, en, reset
  D_Flip_Flop d_ff_6 (.clk(WR), .D(DATAIN[5]), .Q(resultDATAIN[5]));  // open: Qn, preset, en, reset
  D_Flip_Flop d_ff_7 (.clk(WR), .D(DATAIN[6]), .Q(resultDATAIN[6]));  // open: Qn, preset, en, reset
  D_Flip_Flop d_ff_8 (.clk(WR), .D(DATAIN[7]), .Q(resultDATAIN[7]));  // open: Qn, preset, en, reset
  D_Flip_Flop d_ff_9 (.clk(WR), .D(DATAIN[8]), .Q(resultDATAIN[8]));  // open: Qn, preset, en, reset
  D_Flip_Flop d_ff_10 (.clk(WR), .D(DATAIN[9]), .Q(resultDATAIN[9]));  // open: Qn, preset, en, reset
  D_Flip_Flop d_ff_11 (.clk(WR), .D(DATAIN[10]), .Q(resultDATAIN[10]));  // open: Qn, preset, en, reset
  D_Flip_Flop d_ff_12 (.clk(WR), .D(DATAIN[11]), .Q(resultDATAIN[11]));  // open: Qn, preset, en, reset
  D_Flip_Flop d_ff_13 (.clk(WR), .D(DATAIN[12]), .Q(resultDATAIN[12]));  // open: Qn, preset, en, reset
  D_Flip_Flop d_ff_14 (.clk(WR), .D(DATAIN[13]), .Q(resultDATAIN[13]));  // open: Qn, preset, en, reset
  D_Flip_Flop d_ff_15 (.clk(WR), .D(DATAIN[14]), .Q(resultDATAIN[14]));  // open: Qn, preset, en, reset
  D_Flip_Flop d_ff_16 (.clk(WR), .D(DATAIN[15]), .Q(resultDATAIN[15]));  // open: Qn, preset, en, reset
  D_Flip_Flop d_ff_17 (.clk(WR), .D(DATAIN[16]), .Q(resultDATAIN[16]));  // open: Qn, preset, en, reset
  D_Flip_Flop d_ff_18 (.clk(WR), .D(DATAIN[17]), .Q(resultDATAIN[17]));  // open: Qn, preset, en, reset
  D_Flip_Flop d_ff_19 (.clk(WR), .D(DATAIN[18]), .Q(resultDATAIN[18]));  // open: Qn, preset, en, reset
  D_Flip_Flop d_ff_20 (.clk(WR), .D(DATAIN[19]), .Q(resultDATAIN[19]));  // open: Qn, preset, en, reset
  D_Flip_Flop d_ff_21 (.clk(WR), .D(DATAIN[20]), .Q(resultDATAIN[20]));  // open: Qn, preset, en, reset
  D_Flip_Flop d_ff_22 (.clk(WR), .D(DATAIN[21]), .Q(resultDATAIN[21]));  // open: Qn, preset, en, reset
  D_Flip_Flop d_ff_23 (.clk(WR), .D(DATAIN[22]), .Q(resultDATAIN[22]));  // open: Qn, preset, en, reset
  D_Flip_Flop d_ff_24 (.clk(WR), .D(DATAIN[23]), .Q(resultDATAIN[23]));  // open: Qn, preset, en, reset
  D_Flip_Flop d_ff_25 (.clk(WR), .D(DATAIN[24]), .Q(resultDATAIN[24]));  // open: Qn, preset, en, reset
  D_Flip_Flop d_ff_26 (.clk(WR), .D(DATAIN[25]), .Q(resultDATAIN[25]));  // open: Qn, preset, en, reset
  D_Flip_Flop d_ff_27 (.clk(WR), .D(DATAIN[26]), .Q(resultDATAIN[26]));  // open: Qn, preset, en, reset
  D_Flip_Flop d_ff_28 (.clk(WR), .D(DATAIN[27]), .Q(resultDATAIN[27]));  // open: Qn, preset, en, reset
  D_Flip_Flop d_ff_29 (.clk(WR), .D(DATAIN[28]), .Q(resultDATAIN[28]));  // open: Qn, preset, en, reset
  D_Flip_Flop d_ff_30 (.clk(WR), .D(DATAIN[29]), .Q(resultDATAIN[29]));  // open: Qn, preset, en, reset
  D_Flip_Flop d_ff_31 (.clk(WR), .D(DATAIN[30]), .Q(resultDATAIN[30]));  // open: Qn, preset, en, reset
  D_Flip_Flop d_ff_32 (.clk(WR), .D(DATAIN[31]), .Q(resultDATAIN[31]));  // open: Qn, preset, en, reset

  assign DATAOUT = DATAIN;
endmodule

module REG_0 (
  input  [31:0] in_1,
  input  [31:0] S,
  input  [31:0] in_3
);


  assign in_3 = in_1;
  // also tied to GND on the sheet: {S[0], S[1], S[2], S[3], S[4], S[5], S[6], S[7], S[8], S[9], S[10], S[11], S[12], S[13], S[14], S[15], S[16], S[17], S[18], S[19], S[20], S[21], S[22], S[23], S[24], S[25], S[26], S[27], S[28], S[29], S[30], S[31]}
endmodule

module CirCuito_JUMP (
  input  [4:0] OPcode_ULA,
  input  ZERO,
  output JUMP_Program_Counter
);

  wire and_1_out, and_2_out, and_3_out;

  and and_1 (and_1_out, OPcode_ULA[4], OPcode_ULA[3], OPcode_ULA[2], OPcode_ULA[1], OPcode_ULA[0]);
  or or_1 (JUMP_Program_Counter, and_1_out, and_2_out, and_3_out);
  and and_2 (and_2_out, OPcode_ULA[4], OPcode_ULA[3], OPcode_ULA[2], OPcode_ULA[1], ~OPcode_ULA[0], ZERO);  // AND_Gate
  and and_3 (and_3_out, OPcode_ULA[4], OPcode_ULA[3], OPcode_ULA[2], ~OPcode_ULA[1], OPcode_ULA[0], ~ZERO);  // AND_Gate
endmodule

module SomadorADDER (
  input  A,
  input  B,
  input  Cin,
  output Cout,
  output S
);

  wire and_1_out, and_2_out, and_3_out, and_4_out, xor_1_out;

  xor xor_1 (xor_1_out, A, B);
  xor xor_2 (S, Cin, xor_1_out);
  and and_1 (and_1_out, ~Cin, A, B);  // AND_Gate
  and and_2 (and_2_out, Cin, ~A, B);  // AND_Gate
  and and_3 (and_3_out, Cin, A, ~B);  // AND_Gate
  and and_4 (and_4_out, Cin, A, B);
  or or_1 (Cout, and_1_out, and_2_out, and_3_out, and_4_out);
endmodule

module OverFlowCONTROLER (
  input  CoutMSB,
  input  a,
  input  b,
  input  s,
  input  [4:0] OPcode,
  output OverFlow
);

  wire and_1_out, and_2_out, and_3_out, and_4_out, and_5_out, and_6_out, or_1_out, or_2_out;

  Multiplexer #(.enable("false")) multiplexer_1 (.in0(CoutMSB), .in1(or_2_out), .out(OverFlow), .sel(or_1_out));
  or or_1 (or_1_out, and_3_out, and_4_out, and_5_out, and_6_out);
  or or_2 (or_2_out, and_1_out, and_2_out);
  and and_1 (and_1_out, a, b, ~s);  // AND_Gate
  and and_2 (and_2_out, ~a, ~b, s);  // AND_Gate
  and and_3 (and_3_out, ~OPcode[4], OPcode[4], OPcode[4], ~OPcode[4], ~OPcode[4]);  // AND_Gate
  and and_4 (and_4_out, OPcode[4], OPcode[4], ~OPcode[4], OPcode[4], ~OPcode[4]);  // AND_Gate
  and and_5 (and_5_out, ~OPcode[4], OPcode[4], OPcode[4], OPcode[4], OPcode[4]);  // AND_Gate
  and and_6 (and_6_out, OPcode[4], ~OPcode[4], OPcode[4], OPcode[4], OPcode[4]);  // AND_Gate

  assign OPcode[3:0] = {4{OPcode[4]}};
endmodule

module SHIFTER (
  input  A31,
  input  A29,
  input  A27,
  input  A25,
  input  A23,
  input  A21,
  input  A19,
  input  A17,
  input  A15,
  input  A13,
  input  A11,
  input  A9,
  input  A7,
  input  A5,
  input  A3,
  input  A1,
  input  A30,
  input  A28,
  input  A26,
  input  A24,
  input  A22,
  input  A20,
  input  A18,
  input  A16,
  input  A14,
  input  A12,
  input  A10,
  input  A8,
  input  A6,
  input  A4,
  input  A2,
  input  A0,
  input  SHFLEFT,
  input  SHFRIGTH,
  output S31,
  output S29,
  output S27,
  output S25,
  output S23,
  output S21,
  output S19,
  output S17,
  output S15,
  output S13,
  output S11,
  output S9,
  output S7,
  output S5,
  output S3,
  output S1,
  output S30,
  output S28,
  output S26,
  output S24,
  output S22,
  output S20,
  output S18,
  output S16,
  output S14,
  output S12,
  output S10,
  output S8,
  output S6,
  output S4,
  output S2,
  output S0
);

  Multiplexer #(.select(2), .enable("false")) multiplexer_1 (
    .in0(A31), .in1(A30), .in2(1'b0), .out(S31), .sel({SHFRIGTH, SHFLEFT}));  // open: in3
  Multiplexer #(.select(2), .enable("false")) multiplexer_2 (
    .in0(A30), .in1(A29), .in2(A31), .out(S30), .sel({SHFRIGTH, SHFLEFT}));  // open: in3
  Multiplexer #(.select(2), .enable("false")) multiplexer_3 (
    .in0(A29), .in1(A28), .in2(A30), .out(S29), .sel({SHFRIGTH, SHFLEFT}));  // open: in3
  Multiplexer #(.select(2), .enable("false")) multiplexer_4 (
    .in0(A28), .in1(A27), .in2(A29), .out(S28), .sel({SHFRIGTH, SHFLEFT}));  // open: in3
  Multiplexer #(.select(2), .enable("false")) multiplexer_5 (
    .in0(A27), .in1(A26), .in2(A28), .out(S27), .sel({SHFRIGTH, SHFLEFT}));  // open: in3
  Multiplexer #(.select(2), .enable("false")) multiplexer_6 (
    .in0(A26), .in1(A25), .in2(A27), .out(S26), .sel({SHFRIGTH, SHFLEFT}));  // open: in3
  Multiplexer #(.select(2), .enable("false")) multiplexer_7 (
    .in0(A25), .in1(A24), .in2(A26), .out(S25), .sel({SHFRIGTH, SHFLEFT}));  // open: in3
  Multiplexer #(.select(2), .enable("false")) multiplexer_8 (
    .in0(A24), .in1(A23), .in2(A25), .out(S24), .sel({SHFRIGTH, SHFLEFT}));  // open: in3
  Multiplexer #(.select(2), .enable("false")) multiplexer_9 (
    .in0(A23), .in1(A22), .in2(A24), .out(S23), .sel({SHFRIGTH, SHFLEFT}));  // open: in3
  Multiplexer #(.select(2), .enable("false")) multiplexer_10 (
    .in0(A22), .in1(A21), .in2(A23), .out(S22), .sel({SHFRIGTH, SHFLEFT}));  // open: in3
  Multiplexer #(.select(2), .enable("false")) multiplexer_11 (
    .in0(A21), .in1(A20), .in2(A22), .out(S21), .sel({SHFRIGTH, SHFLEFT}));  // open: in3
  Multiplexer #(.select(2), .enable("false")) multiplexer_12 (
    .in0(A20), .in1(A19), .in2(A21), .out(S20), .sel({SHFRIGTH, SHFLEFT}));  // open: in3
  Multiplexer #(.select(2), .enable("false")) multiplexer_13 (
    .in0(A19), .in1(A18), .in2(A20), .out(S19), .sel({SHFRIGTH, SHFLEFT}));  // open: in3
  Multiplexer #(.select(2), .enable("false")) multiplexer_14 (
    .in0(A18), .in1(A17), .in2(A19), .out(S18), .sel({SHFRIGTH, SHFLEFT}));  // open: in3
  Multiplexer #(.select(2), .enable("false")) multiplexer_15 (
    .in0(A17), .in1(A16), .in2(A18), .out(S17), .sel({SHFRIGTH, SHFLEFT}));  // open: in3
  Multiplexer #(.select(2), .enable("false")) multiplexer_16 (
    .in0(A16), .in1(A15), .in2(A17), .out(S16), .sel({SHFRIGTH, SHFLEFT}));  // open: in3
  Multiplexer #(.select(2), .enable("false")) multiplexer_17 (
    .in0(A15), .in1(A14), .in2(A16), .out(S15), .sel({SHFRIGTH, SHFLEFT}));  // open: in3
  Multiplexer #(.select(2), .enable("false")) multiplexer_18 (
    .in0(A14), .in1(A13), .in2(A15), .out(S14), .sel({SHFRIGTH, SHFLEFT}));  // open: in3
  Multiplexer #(.select(2), .enable("false")) multiplexer_19 (
    .in0(A13), .in1(A12), .in2(A14), .out(S13), .sel({SHFRIGTH, SHFLEFT}));  // open: in3
  Multiplexer #(.select(2), .enable("false")) multiplexer_20 (
    .in0(A12), .in1(A11), .in2(A13), .out(S12), .sel({SHFRIGTH, SHFLEFT}));  // open: in3
  Multiplexer #(.select(2), .enable("false")) multiplexer_21 (
    .in0(A11), .in1(A10), .in2(A12), .out(S11), .sel({SHFRIGTH, SHFLEFT}));  // open: in3
  Multiplexer #(.select(2), .enable("false")) multiplexer_22 (
    .in0(A10), .in1(A9), .in2(A11), .out(S10), .sel({SHFRIGTH, SHFLEFT}));  // open: in3
  Multiplexer #(.select(2), .enable("false")) multiplexer_23 (
    .in0(A9), .in1(A8), .in2(A10), .out(S9), .sel({SHFRIGTH, SHFLEFT}));  // open: in3
  Multiplexer #(.select(2), .enable("false")) multiplexer_24 (
    .in0(A8), .in1(A7), .in2(A9), .out(S8), .sel({SHFRIGTH, SHFLEFT}));  // open: in3
  Multiplexer #(.select(2), .enable("false")) multiplexer_25 (
    .in0(A7), .in1(A6), .in2(A8), .out(S7), .sel({SHFRIGTH, SHFLEFT}));  // open: in3
  Multiplexer #(.select(2), .enable("false")) multiplexer_26 (
    .in0(A6), .in1(A5), .in2(A7), .out(S6), .sel({SHFRIGTH, SHFLEFT}));  // open: in3
  Multiplexer #(.select(2), .enable("false")) multiplexer_27 (
    .in0(A5), .in1(A4), .in2(A6), .out(S5), .sel({SHFRIGTH, SHFLEFT}));  // open: in3
  Multiplexer #(.select(2), .enable("false")) multiplexer_28 (
    .in0(A4), .in1(A3), .in2(A5), .out(S4), .sel({SHFRIGTH, SHFLEFT}));  // open: in3
  Multiplexer #(.select(2), .enable("false")) multiplexer_29 (
    .in0(A3), .in1(A2), .in2(A4), .out(S3), .sel({SHFRIGTH, SHFLEFT}));  // open: in3
  Multiplexer #(.select(2), .enable("false")) multiplexer_30 (
    .in0(A2), .in1(A1), .in2(A3), .out(S2), .sel({SHFRIGTH, SHFLEFT}));  // open: in3
  Multiplexer #(.select(2), .enable("false")) multiplexer_31 (
    .in0(A1), .in1(A0), .in2(A2), .out(S1), .sel({SHFRIGTH, SHFLEFT}));  // open: in3
  Multiplexer #(.select(2), .enable("false")) multiplexer_32 (
    .in0(A0), .in1(1'b0), .in2(A1), .out(S0), .sel({SHFRIGTH, SHFLEFT}));  // open: in3
endmodule

module SHIFTER_ARITIMETICO (
  input  A31,
  input  A29,
  input  A27,
  input  A25,
  input  A23,
  input  A21,
  input  A19,
  input  A17,
  input  A15,
  input  A13,
  input  A11,
  input  A9,
  input  A7,
  input  A5,
  input  A3,
  input  A1,
  input  A30,
  input  A28,
  input  A26,
  input  A24,
  input  A22,
  input  A20,
  input  A18,
  input  A16,
  input  A14,
  input  A12,
  input  A10,
  input  A8,
  input  A6,
  input  A4,
  input  A2,
  input  A0,
  input  in_33,
  output S31,
  output S29,
  output S27,
  output S25,
  output S23,
  output S21,
  output S19,
  output S17,
  output S15,
  output S13,
  output S11,
  output S9,
  output S7,
  output S5,
  output S3,
  output S1,
  output S30,
  output S28,
  output S26,
  output S24,
  output S22,
  output S20,
  output S18,
  output S16,
  output S14,
  output S12,
  output S10,
  output S8,
  output S6,
  output S4,
  output S2,
  output S0
);

  Multiplexer #(.select(2), .enable("false")) multiplexer_1 (
    .in0(A31), .in1(A30), .in2(A31), .out(S31), .sel({in_33, 1'b0}));  // open: in3
  Multiplexer #(.select(2), .enable("false")) multiplexer_2 (
    .in0(A30), .in1(A29), .in2(A31), .out(S30), .sel({in_33, 1'b0}));  // open: in3
  Multiplexer #(.select(2), .enable("false")) multiplexer_3 (
    .in0(A29), .in1(A28), .in2(A30), .out(S29), .sel({in_33, 1'b0}));  // open: in3
  Multiplexer #(.select(2), .enable("false")) multiplexer_4 (
    .in0(A28), .in1(A27), .in2(A29), .out(S28), .sel({in_33, 1'b0}));  // open: in3
  Multiplexer #(.select(2), .enable("false")) multiplexer_5 (
    .in0(A27), .in1(A26), .in2(A28), .out(S27), .sel({in_33, 1'b0}));  // open: in3
  Multiplexer #(.select(2), .enable("false")) multiplexer_6 (
    .in0(A26), .in1(A25), .in2(A27), .out(S26), .sel({in_33, 1'b0}));  // open: in3
  Multiplexer #(.select(2), .enable("false")) multiplexer_7 (
    .in0(A25), .in1(A24), .in2(A26), .out(S25), .sel({in_33, 1'b0}));  // open: in3
  Multiplexer #(.select(2), .enable("false")) multiplexer_8 (
    .in0(A24), .in1(A23), .in2(A25), .out(S24), .sel({in_33, 1'b0}));  // open: in3
  Multiplexer #(.select(2), .enable("false")) multiplexer_9 (
    .in0(A23), .in1(A22), .in2(A24), .out(S23), .sel({in_33, 1'b0}));  // open: in3
  Multiplexer #(.select(2), .enable("false")) multiplexer_10 (
    .in0(A22), .in1(A21), .in2(A23), .out(S22), .sel({in_33, 1'b0}));  // open: in3
  Multiplexer #(.select(2), .enable("false")) multiplexer_11 (
    .in0(A21), .in1(A20), .in2(A22), .out(S21), .sel({in_33, 1'b0}));  // open: in3
  Multiplexer #(.select(2), .enable("false")) multiplexer_12 (
    .in0(A20), .in1(A19), .in2(A21), .out(S20), .sel({in_33, 1'b0}));  // open: in3
  Multiplexer #(.select(2), .enable("false")) multiplexer_13 (
    .in0(A19), .in1(A18), .in2(A20), .out(S19), .sel({in_33, 1'b0}));  // open: in3
  Multiplexer #(.select(2), .enable("false")) multiplexer_14 (
    .in0(A18), .in1(A17), .in2(A19), .out(S18), .sel({in_33, 1'b0}));  // open: in3
  Multiplexer #(.select(2), .enable("false")) multiplexer_15 (
    .in0(A17), .in1(A16), .in2(A18), .out(S17), .sel({in_33, 1'b0}));  // open: in3
  Multiplexer #(.select(2), .enable("false")) multiplexer_16 (
    .in0(A16), .in1(A15), .in2(A17), .out(S16), .sel({in_33, 1'b0}));  // open: in3
  Multiplexer #(.select(2), .enable("false")) multiplexer_17 (
    .in0(A15), .in1(A14), .in2(A16), .out(S15), .sel({in_33, 1'b0}));  // open: in3
  Multiplexer #(.select(2), .enable("false")) multiplexer_18 (
    .in0(A14), .in1(A13), .in2(A15), .out(S14), .sel({in_33, 1'b0}));  // open: in3
  Multiplexer #(.select(2), .enable("false")) multiplexer_19 (
    .in0(A13), .in1(A12), .in2(A14), .out(S13), .sel({in_33, 1'b0}));  // open: in3
  Multiplexer #(.select(2), .enable("false")) multiplexer_20 (
    .in0(A12), .in1(A11), .in2(A13), .out(S12), .sel({in_33, 1'b0}));  // open: in3
  Multiplexer #(.select(2), .enable("false")) multiplexer_21 (
    .in0(A11), .in1(A10), .in2(A12), .out(S11), .sel({in_33, 1'b0}));  // open: in3
  Multiplexer #(.select(2), .enable("false")) multiplexer_22 (
    .in0(A10), .in1(A9), .in2(A11), .out(S10), .sel({in_33, 1'b0}));  // open: in3
  Multiplexer #(.select(2), .enable("false")) multiplexer_23 (
    .in0(A9), .in1(A8), .in2(A10), .out(S9), .sel({in_33, 1'b0}));  // open: in3
  Multiplexer #(.select(2), .enable("false")) multiplexer_24 (
    .in0(A8), .in1(A7), .in2(A9), .out(S8), .sel({in_33, 1'b0}));  // open: in3
  Multiplexer #(.select(2), .enable("false")) multiplexer_25 (
    .in0(A7), .in1(A6), .in2(A8), .out(S7), .sel({in_33, 1'b0}));  // open: in3
  Multiplexer #(.select(2), .enable("false")) multiplexer_26 (
    .in0(A6), .in1(A5), .in2(A7), .out(S6), .sel({in_33, 1'b0}));  // open: in3
  Multiplexer #(.select(2), .enable("false")) multiplexer_27 (
    .in0(A5), .in1(A4), .in2(A6), .out(S5), .sel({in_33, 1'b0}));  // open: in3
  Multiplexer #(.select(2), .enable("false")) multiplexer_28 (
    .in0(A4), .in1(A3), .in2(A5), .out(S4), .sel({in_33, 1'b0}));  // open: in3
  Multiplexer #(.select(2), .enable("false")) multiplexer_29 (
    .in0(A3), .in1(A2), .in2(A4), .out(S3), .sel({in_33, 1'b0}));  // open: in3
  Multiplexer #(.select(2), .enable("false")) multiplexer_30 (
    .in0(A2), .in1(A1), .in2(A3), .out(S2), .sel({in_33, 1'b0}));  // open: in3
  Multiplexer #(.select(2), .enable("false")) multiplexer_31 (
    .in0(A1), .in1(A0), .in2(A2), .out(S1), .sel({in_33, 1'b0}));  // open: in3
  Multiplexer #(.select(2), .enable("false")) multiplexer_32 (
    .in0(A0), .in1(1'b0), .in2(A1), .out(S0), .sel({in_33, 1'b0}));  // open: in3
endmodule

module ROL (
  input  A31,
  input  A29,
  input  A27,
  input  A25,
  input  A23,
  input  A21,
  input  A19,
  input  A17,
  input  A15,
  input  A13,
  input  A11,
  input  A9,
  input  A7,
  input  A5,
  input  A3,
  input  A1,
  input  A30,
  input  A28,
  input  A26,
  input  A24,
  input  A22,
  input  A20,
  input  A18,
  input  A16,
  input  A14,
  input  A12,
  input  A10,
  input  A8,
  input  A6,
  input  A4,
  input  A2,
  input  A0,
  input  in_33,
  output S31,
  output S29,
  output S27,
  output S25,
  output S23,
  output S21,
  output S19,
  output S17,
  output S15,
  output S13,
  output S11,
  output S9,
  output S7,
  output S5,
  output S3,
  output S1,
  output S30,
  output S28,
  output S26,
  output S24,
  output S22,
  output S20,
  output S18,
  output S16,
  output S14,
  output S12,
  output S10,
  output S8,
  output S6,
  output S4,
  output S2,
  output S0
);

  Multiplexer #(.select(2), .enable("false")) multiplexer_1 (
    .in0(A31), .in1(A30), .in2(1'b0), .out(S31), .sel({in_33, 1'b0}));  // open: in3
  Multiplexer #(.select(2), .enable("false")) multiplexer_2 (
    .in0(A30), .in1(A29), .in2(A31), .out(S30), .sel({in_33, 1'b0}));  // open: in3
  Multiplexer #(.select(2), .enable("false")) multiplexer_3 (
    .in0(A29), .in1(A28), .in2(A30), .out(S29), .sel({in_33, 1'b0}));  // open: in3
  Multiplexer #(.select(2), .enable("false")) multiplexer_4 (
    .in0(A28), .in1(A27), .in2(A29), .out(S28), .sel({in_33, 1'b0}));  // open: in3
  Multiplexer #(.select(2), .enable("false")) multiplexer_5 (
    .in0(A27), .in1(A26), .in2(A28), .out(S27), .sel({in_33, 1'b0}));  // open: in3
  Multiplexer #(.select(2), .enable("false")) multiplexer_6 (
    .in0(A26), .in1(A25), .in2(A27), .out(S26), .sel({in_33, 1'b0}));  // open: in3
  Multiplexer #(.select(2), .enable("false")) multiplexer_7 (
    .in0(A25), .in1(A24), .in2(A26), .out(S25), .sel({in_33, 1'b0}));  // open: in3
  Multiplexer #(.select(2), .enable("false")) multiplexer_8 (
    .in0(A24), .in1(A23), .in2(A25), .out(S24), .sel({in_33, 1'b0}));  // open: in3
  Multiplexer #(.select(2), .enable("false")) multiplexer_9 (
    .in0(A23), .in1(A22), .in2(A24), .out(S23), .sel({in_33, 1'b0}));  // open: in3
  Multiplexer #(.select(2), .enable("false")) multiplexer_10 (
    .in0(A22), .in1(A21), .in2(A23), .out(S22), .sel({in_33, 1'b0}));  // open: in3
  Multiplexer #(.select(2), .enable("false")) multiplexer_11 (
    .in0(A21), .in1(A20), .in2(A22), .out(S21), .sel({in_33, 1'b0}));  // open: in3
  Multiplexer #(.select(2), .enable("false")) multiplexer_12 (
    .in0(A20), .in1(A19), .in2(A21), .out(S20), .sel({in_33, 1'b0}));  // open: in3
  Multiplexer #(.select(2), .enable("false")) multiplexer_13 (
    .in0(A19), .in1(A18), .in2(A20), .out(S19), .sel({in_33, 1'b0}));  // open: in3
  Multiplexer #(.select(2), .enable("false")) multiplexer_14 (
    .in0(A18), .in1(A17), .in2(A19), .out(S18), .sel({in_33, 1'b0}));  // open: in3
  Multiplexer #(.select(2), .enable("false")) multiplexer_15 (
    .in0(A17), .in1(A16), .in2(A18), .out(S17), .sel({in_33, 1'b0}));  // open: in3
  Multiplexer #(.select(2), .enable("false")) multiplexer_16 (
    .in0(A16), .in1(A15), .in2(A17), .out(S16), .sel({in_33, 1'b0}));  // open: in3
  Multiplexer #(.select(2), .enable("false")) multiplexer_17 (
    .in0(A15), .in1(A14), .in2(A16), .out(S15), .sel({in_33, 1'b0}));  // open: in3
  Multiplexer #(.select(2), .enable("false")) multiplexer_18 (
    .in0(A14), .in1(A13), .in2(A15), .out(S14), .sel({in_33, 1'b0}));  // open: in3
  Multiplexer #(.select(2), .enable("false")) multiplexer_19 (
    .in0(A13), .in1(A12), .in2(A14), .out(S13), .sel({in_33, 1'b0}));  // open: in3
  Multiplexer #(.select(2), .enable("false")) multiplexer_20 (
    .in0(A12), .in1(A11), .in2(A13), .out(S12), .sel({in_33, 1'b0}));  // open: in3
  Multiplexer #(.select(2), .enable("false")) multiplexer_21 (
    .in0(A11), .in1(A10), .in2(A12), .out(S11), .sel({in_33, 1'b0}));  // open: in3
  Multiplexer #(.select(2), .enable("false")) multiplexer_22 (
    .in0(A10), .in1(A9), .in2(A11), .out(S10), .sel({in_33, 1'b0}));  // open: in3
  Multiplexer #(.select(2), .enable("false")) multiplexer_23 (
    .in0(A9), .in1(A8), .in2(A10), .out(S9), .sel({in_33, 1'b0}));  // open: in3
  Multiplexer #(.select(2), .enable("false")) multiplexer_24 (
    .in0(A8), .in1(A7), .in2(A9), .out(S8), .sel({in_33, 1'b0}));  // open: in3
  Multiplexer #(.select(2), .enable("false")) multiplexer_25 (
    .in0(A7), .in1(A6), .in2(A8), .out(S7), .sel({in_33, 1'b0}));  // open: in3
  Multiplexer #(.select(2), .enable("false")) multiplexer_26 (
    .in0(A6), .in1(A5), .in2(A7), .out(S6), .sel({in_33, 1'b0}));  // open: in3
  Multiplexer #(.select(2), .enable("false")) multiplexer_27 (
    .in0(A5), .in1(A4), .in2(A6), .out(S5), .sel({in_33, 1'b0}));  // open: in3
  Multiplexer #(.select(2), .enable("false")) multiplexer_28 (
    .in0(A4), .in1(A3), .in2(A5), .out(S4), .sel({in_33, 1'b0}));  // open: in3
  Multiplexer #(.select(2), .enable("false")) multiplexer_29 (
    .in0(A3), .in1(A2), .in2(A4), .out(S3), .sel({in_33, 1'b0}));  // open: in3
  Multiplexer #(.select(2), .enable("false")) multiplexer_30 (
    .in0(A2), .in1(A1), .in2(A3), .out(S2), .sel({in_33, 1'b0}));  // open: in3
  Multiplexer #(.select(2), .enable("false")) multiplexer_31 (
    .in0(A1), .in1(A0), .in2(A2), .out(S1), .sel({in_33, 1'b0}));  // open: in3
  Multiplexer #(.select(2), .enable("false")) multiplexer_32 (
    .in0(A0), .in1(A31), .in2(A1), .out(S0), .sel({in_33, 1'b0}));  // open: in3
endmodule

module Gambiarra_12___32 (
  input  [31:0] in_1,
  output [11:0] out_2
);


  assign in_1[30:11] = {20{in_1[31]}};
  assign out_2 = {in_1[31], in_1[10:0]};
endmodule
